# Fritzing sketch cociclo (saved by Fritzing 0.9.0b)
circuit board: 5.4cm x 3.4cm
breadboards: 1

parts:
  VCC1 = Battery block 9V
  Pad24 = Pad [width=3.30665666666667 height=1.4116670888889 connect=center]  # not connected
  U1 = SPDT Slide Switch [package=ayz0202]
  MH7 = GAS_SENSOR [package=mq-3]
  Pad25 = Pad [width=2.67165666666667 height=0.964815237037042 connect=center]  # not connected
  C6 = Electrolytic Capacitor [capacitance=10µF package="0405 [SMD, electrolytic]"]
  C5 = Electrolytic Capacitor [capacitance=10µF package="0405 [SMD, electrolytic]"]
  Pad15 = Pad [width=2.95387888888889 height=1.34111153333333 connect=center]  # not connected
  Pad16 = Pad [width=3.30665666666667 height=1.4116670888889 connect=center]
  LED1 = smd LED [color="Red (633nm)" package="1206 [SMD]"]
  220 = Resistor [tolerance=±5% resistance=220 package="1206 [SMD]"]
  J4 = female pin header, 2 pins [form="♀ (female)"]
  R1 = Resistor [tolerance=±5% resistance=220 package="1206 [SMD]"]
  R2 = Resistor [tolerance=±5% resistance=220 package="1206 [SMD]"]
  C7 = Ceramic Capacitor [capacitance=1nF package="1206 [SMD, multilayer]"]
  D5-10 = female pin header, 2 pins [form="♀ (female)"]
  R3 = Resistor [tolerance=±5% resistance=220 package="1206 [SMD]"]
  R4 = Resistor [tolerance=±5% resistance=10k package="1206 [SMD]"]
  Pad20 = Pad [width=2.53999999999998 height=2.63407407407408 connect=center]
  Pad21 = Pad [width=2.53999999999998 height=2.63407407407408 connect=center]
  Pad23 = Pad [width=4.23334274074075 height=5.73852792592593 connect=center]
  R5 = Resistor [tolerance=±5% resistance=10k package="1206 [SMD]"]
  ATMEGA168 = atmega168 [package=dip]
  J5 = female pin header, 4 pins [form="♀ (female)"]
  U3 = Voltage Regulator [package=sot223]
  Pad26 = Pad [width=1.09121222222223 height=1.51044486666667 connect=center]  # not connected
  Pad27 = Pad [width=1.09121222222223 height=1.51044486666667 connect=center]  # not connected
  Pad28 = Pad [width=1.09121222222223 height=1.51044486666667 connect=center]  # not connected
  Pad29 = Pad [width=1.09121222222223 height=1.51044486666667 connect=center]  # not connected

nets:
  N1: VCC1.-, C6.-, C5.-, Pad16.pad, LED1.anode, Pad23.pad, ATMEGA168.GND#7
  N2: VCC1.+, U1.5
  N3: U1.6, C5.+, U3.Vin
  N4: MH7.B1, MH7.H2, 220.Pin_0, R3.Pin_0, Pad21.pad, R5.Pin_0, ATMEGA168.VCC, ATMEGA168.AVCC, ATMEGA168.AREF, U3.Vout_5V
  N5: MH7.A1, ATMEGA168.A0
  N6: MH7.H1, R2.Pin_0, D5-10.pin2, R4.Pin_1, ATMEGA168.GND#21, J5.pin3
  N7: LED1.cathode, 220.Pin_1
  N8: J4.pin1, C7.0
  N9: J4.pin2, R1.Pin_1, ATMEGA168.D3_(PWM)
  N10: R1.Pin_0, R2.Pin_1, C7.1
  N11: D5-10.pin1, R3.Pin_1, ATMEGA168.A1
  N12: R4.Pin_0, Pad20.pad
  N13: R5.Pin_1, ATMEGA168.RESET
  N14: ATMEGA168.D9_(PWM), J5.pin1
  N15: ATMEGA168.D10_(PWM), J5.pin2
  N16: ATMEGA168.D11_(PWM), J5.pin4

custom parts:
  Voltage Regulator: Voltage Regulator Standard LM317 adjustable voltage regulator. AOI (Adjust Output Input). Google 'LM317 Calculator' for easy to use app to get the two resistor values needed. 240/720 for 5V output. 240/390 for 3.3V output. Spark Fun Electronics SKU : COM-00527
